# Fritzing sketch 6-Dof-robot-arm-schematic (saved by Fritzing 0.9.9b)

parts:
  Part1 = Arduino Uno (Rev3) - ICSP
  DC1 = DC_DC_XL4016 [package=board_screw]
  J1 = Basic Servo
  PWM1 = PCA9685 16x12-bit PWM Breakout
  J2 = Basic Servo
  J3 = Basic Servo
  J4 = Basic Servo
  J5 = Basic Servo
  J6 = Basic Servo
  J8 = Power Jack [package=power_jack_slot]
  J9 = Dagu DGServo 9g header (male) [package=THT]
  J10 = Dagu DGServo 9g header (male) [package=THT]
  J11 = Dagu DGServo 9g header (male) [package=THT]
  J12 = Dagu DGServo 9g header (male) [package=THT]
  J13 = Dagu DGServo 9g header (male) [package=THT]
  J14 = Dagu DGServo 9g header (male) [package=THT]
  J15 = Dagu DGServo 9g header (male) [package=THT]
  JACK1 = 2.1mm Barrel Jack with Terminal Block
  HLK-PM1 = HLK-PM12 [part_number=GACUN-1260]

nets:
  N1: Part1.GND, DC1.OUT-, PWM1.no_name_yet#501, PWM1.no_name_yet#701, PWM1.no_name_yet#1000, PWM1.no_name_yet#1001, PWM1.no_name_yet#1002, PWM1.no_name_yet#1003, PWM1.no_name_yet#1004, PWM1.no_name_yet#1005, PWM1.no_name_yet#1006
  N2: Part1.A4/SDA, PWM1.no_name_yet#504
  N3: Part1.A5/SCL, PWM1.no_name_yet#503
  N4: Part1.5V, PWM1.no_name_yet#505
  N5: DC1.IN+, J8.PWR
  N6: DC1.IN-, J8.GND
  N7: DC1.OUT+, PWM1.no_name_yet#100, PWM1.no_name_yet#101, PWM1.no_name_yet#102, PWM1.no_name_yet#103, PWM1.no_name_yet#104, PWM1.no_name_yet#105, PWM1.no_name_yet#106, PWM1.no_name_yet#706
  GND: J1.gnd, J13.gnd
  VCC: J1.vcc, J13.Vcc
  N8: J1.pulse, PWM1.no_name_yet#4, J13.pulse
  N9: PWM1.no_name_yet#0, J6.pulse, J9.pulse
  N10: PWM1.no_name_yet#1, J5.pulse, J10.pulse
  N11: PWM1.no_name_yet#2, J4.pulse, J11.pulse
  N12: PWM1.no_name_yet#3, J3.pulse, J12.pulse
  N13: PWM1.no_name_yet#5, J2.pulse, J14.pulse
  N14: PWM1.no_name_yet#6, J15.pulse
  GND_2: J2.gnd, J14.gnd
  VCC_2: J2.vcc, J14.Vcc
  GND_3: J3.gnd, J12.gnd
  VCC_3: J3.vcc, J12.Vcc
  GND_4: J4.gnd, J11.gnd
  VCC_4: J4.vcc, J11.Vcc
  GND_5: J5.gnd, J10.gnd
  VCC_5: J5.vcc, J10.Vcc
  GND_6: J6.gnd, J9.gnd
  VCC_6: J6.vcc, J9.Vcc
  N15: JACK1.POS, HLK-PM1.+Vo
  N16: JACK1.NEG, HLK-PM1.-Vo

notes:
  Power supply:
  Gacun-1260
  Input: 110-240V
  Output: 12Vdc. 6.0A
  Step down converter:
  Input: 12 Vdc. 6.0A
  Output: 6 Vdc. 6.0A
  Servo 0:
  Rotating base
  Servo 1:
  Shoulder
  Servo2:
  First elbow
  Servo 3:
  Second elbow
  Servo 4:
  Wrist
  Servo 5:
  Hand (Gripper)
